# Fritzing sketch ina228_i2c (saved by Fritzing 1.0.5)
breadboards: 1

parts:
  Pico_H4 = Raspberry Pi Pico H
  Pico_H3 = Raspberry Pi Pico H
  Adafruit_INA228_I2C_Power_Monitor2 = Adafruit INA228 I2C Power Monitor [part_number=#5832]

nets:
  N1: Pico_H4.VSYS, Adafruit_INA228_I2C_Power_Monitor2.VIN-
  GND: Pico_H4.GND, Pico_H3.GND, Adafruit_INA228_I2C_Power_Monitor2.GND
  N2: Pico_H3.VSYS, Adafruit_INA228_I2C_Power_Monitor2.VCC, Adafruit_INA228_I2C_Power_Monitor2.VBUS, Adafruit_INA228_I2C_Power_Monitor2.VIN+
  N3: Pico_H3.GP5, Adafruit_INA228_I2C_Power_Monitor2.SCL
  N4: Pico_H3.GP4, Adafruit_INA228_I2C_Power_Monitor2.SDA

notes:
  High side power measurement using ina228
  analyser device
  powered by usb
  powered by analyser
  device under test

custom parts:
  Raspberry Pi Pico H: Raspberry Pi Pico H. Based around the RP2040 microcontroller the Pico H is a low cost microcontroller device bringing Raspberry Pi quality, cost, and easy of use to the microcontroller space.
  Adafruit INA228 I2C Power Monitor: The INA228 is an amazing power monitoring chip, with best-of-everything support: up to 85VDC common-mode, high or low side measurements, 20-bit (!) ADC for precision measurements from milliamp to Amp, and I2C interface for easy configuration of alerts, oversampling, gain adjustments and more! This breakout board may well be the last current sensing solution you every need to buy. Not only can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
